# Fritzing sketch diagrama_eletrico (saved by Fritzing 1.0.2b)
breadboards: 1

parts:
  Part1 = Arduino Mega 2560 (Rev3)
  R1 = Resistor Mini [tolerance=±5% resistance=10k package=THT]
  R2 = Resistor Mini [tolerance=±5% resistance=330 package=THT]
  R4 = Resistor Mini [tolerance=±5% resistance=330 package=THT]
  S1 = Momentary Switch [package=ksa_sealed_tac_switch]
  LED1 = LED - 5mm [color="Green (555nm)" current=0.030A package="5 mm [THT]"]
  LED3 = LED - 5mm [color="White (8000K)" current=0.030A package="5 mm [THT]"]
  LED4 = LED - 5mm [color="Infrared (940nm)" current=0.030A package="5 mm [THT]"]
  R5 = Resistor Mini [tolerance=±5% resistance=10k package=THT]

nets:
  N1: Part1.A1, LED4.anode, R5.Pin_0
  N2: Part1.5V, R2.Pin_1, S1.3, R5.Pin_1
  N3: Part1.GND, R1.Pin_0, LED1.anode, LED3.cathode, LED4.cathode
  N4: Part1.D2_PWM, S1.1
  N5: Part1.D3_PWM, R4.Pin_0
  N6: R1.Pin_1, S1.2
  N7: R2.Pin_0, LED3.anode
  N8: R4.Pin_1, LED1.cathode

custom parts:
  Resistor Mini: A generic resistor (0.25W)
